// Logisim project mcdxxxiini.circ as structural Verilog
module arithmetic_unit (
  input  ic,
  input  op2,
  input  op1,
  input  op0,
  input  [31:0] X,
  input  [31:0] Y,
  output [3:0] flags,
  output [31:0] Xout,
  output [31:0] Yout
);

  wire adder_1_cout;
  wire [4:0] bit_extender_1_out;
  wire [31:0] adder_1_out, divider_1_out, divider_1_rem, multiplier_1_cout, multiplier_1_out, negator_1_out,
       shifter_1_out, shifter_2_out, subtractor_1_out, undriven;

  Adder #(.width(32)) adder_1 (.a(X), .b(Y), .out(adder_1_out), .cout(adder_1_cout));  // open: cin
  Subtractor #(.width(32)) subtractor_1 (.a(X), .b(Y), .out(subtractor_1_out));  // open: bin, bout
  Multiplier #(.mode("twosComplement"), .width(32)) multiplier_1 (
    .a(X), .b(Y), .out(multiplier_1_out), .cout(multiplier_1_cout));  // open: cin
  Divider #(.mode("twosComplement"), .width(32)) divider_1 (
    .a(X), .b(Y), .out(divider_1_out), .rem(divider_1_rem));  // open: upper
  Bit_Extender #(.in_width(32), .out_width(5), .\type ("zero")) bit_extender_1 (.in(Y), .out(bit_extender_1_out));
  Negator #(.width(32)) negator_1 (.in(X), .out(negator_1_out));
  Shifter #(.width(32)) shifter_1 (.in(X), .\dist (bit_extender_1_out), .out(shifter_1_out));
  Shifter #(.shift("lr"), .width(32)) shifter_2 (.in(X), .\dist (bit_extender_1_out), .out(shifter_2_out));
  Multiplexer #(.select(3), .width(32)) multiplexer_1 (
    .in0(X), .in1(adder_1_out), .in2(subtractor_1_out), .in3(multiplier_1_out), .in4(divider_1_out),
    .in5(negator_1_out), .in6(shifter_1_out), .in7(shifter_2_out), .out({flags[0], Xout[30:0]}),
    .sel({op2, op1, op0}));
  Comparator #(.width(32)) comparator_1 (.a(X), .b(Y), .eq(flags[1]));  // open: gt, lt
  Multiplexer #(.select(3), .width(32)) multiplexer_2 (
    .in0({32{1'b0}}), .in1({32{1'b0}}), .in2({32{1'b0}}), .in3(undriven), .in4(multiplier_1_cout),
    .in5(divider_1_rem), .in6({32{1'b0}}), .in7({32{1'b0}}), .out(Yout), .sel({op2, op1, op0}));
  Multiplexer #(.select(3)) multiplexer_3 (
    .in0(1'b0), .in1(adder_1_cout), .in2(1'b0), .in3(1'b0), .in4(1'b0), .in5(1'b0), .in6(1'b0), .in7(1'b0),
    .out(flags[2]), .sel({op2, op1, op0}));

  assign flags[3] = ic;
  assign Xout[31] = flags[0];
endmodule

module logical_unit (
  input  ic,
  input  cf,
  input  op2,
  input  op1,
  input  op0,
  input  [31:0] X,
  input  [31:0] Y,
  output [3:0] flags,
  output [31:0] Xout,
  output [31:0] Yout
);

  wire [31:0] and_1_out, nand_1_out, nor_1_out, not_1_out, or_1_out, xnor_1_out, xor_1_out;

  assign and_1_out = X & Y;  // AND_Gate and_1, 32 bits wide
  assign or_1_out = X | Y;  // OR_Gate or_1, 32 bits wide
  assign nand_1_out = ~(X & Y);  // NAND_Gate nand_1, 32 bits wide
  assign nor_1_out = ~(X | Y);  // NOR_Gate nor_1, 32 bits wide
  assign not_1_out = ~X;  // NOT_Gate not_1, 32 bits wide
  assign xor_1_out = X ^ Y;  // XOR_Gate xor_1, 32 bits wide
  Multiplexer #(.select(3), .width(32)) multiplexer_1 (
    .in0(X), .in1(and_1_out), .in2(or_1_out), .in3(nand_1_out), .in4(nor_1_out), .in5(not_1_out),
    .in6(xor_1_out), .in7(xnor_1_out), .out(Xout), .sel({op2, op1, op0}));
  assign xnor_1_out = ~(X ^ Y);  // XNOR_Gate xnor_1, 32 bits wide
  Comparator #(.width(32)) comparator_1 (.a(Xout), .b({32{1'b0}}), .eq(flags[1]), .lt(flags[0]));  // open: gt

  assign flags[3:2] = {ic, cf};
  assign Yout = {32{1'b0}};
endmodule
